// Logisim project Gray_Code.circ as structural Verilog: 1 circuit, main circuit main
module main (
  input  g3,
  input  B3,
  input  g2,
  input  B2,
  input  g1,
  input  B1,
  input  g0,
  input  B0,
  output b3_2,
  output G3_2,
  output b2_2,
  output G2_2,
  output b1_2,
  output G1_2,
  output b0_2,
  output G0_2
);

  xor xor_1 (G2_2, B3, B2);
  xor xor_2 (G1_2, B2, B1);
  xor xor_3 (G0_2, B1, B0);
  xor xor_4 (b2_2, g3, g2);
  xor xor_5 (b1_2, b2_2, g1);
  xor xor_6 (b0_2, b1_2, g0);

  assign b3_2 = g3;
  assign G3_2 = B3;

  // Notes on the sheet:
  //   Binary to Gray Code
  //   Gray Code to Binary
endmodule
