// Logisim project JK_Sequence_Gray_Code.circ as structural Verilog: 1 circuit, main circuit main
module main (
);

  wire and_1_out, and_2_out, and_3_out, and_4_out, and_5_out, and_6_out, and_7_out, and_8_out, and_11_out,
       and_14_out, and_15_out, and_16_out, and_17_out, and_18_out, and_19_out, and_20_out, and_21_out,
       and_22_out, and_23_out, and_24_out, and_25_out, clock_1_out, J1, J2, J3, J4, K1, K2, K3, K4, nQ1, nQ2,
       nQ3, nQ4, or_3_out, or_5_out, or_6_out, or_8_out, Q1, Q2, Q3, Q4;

  J_K_Flip_Flop u_Q1 (.J(J1), .clk(clock_1_out), .K(K1), .Q(Q1), .Qn(nQ1));  // open: preset, en, reset
  Clock clock_1 (.out(clock_1_out));
  and and_1 (and_1_out, Q2, nQ3);
  and and_2 (and_2_out, nQ2, nQ3);
  and and_3 (and_3_out, nQ1, Q4);
  and and_4 (and_4_out, Q1, Q4);
  and and_5 (and_5_out, nQ1, nQ2);
  and and_6 (and_6_out, nQ1, Q2);
  and and_7 (and_7_out, Q1, Q2);
  and and_8 (and_8_out, Q1, nQ2);
  J_K_Flip_Flop u_Q2 (.J(J2), .clk(clock_1_out), .K(K2), .Q(Q2), .Qn(nQ2));  // open: preset, en, reset
  and and_9 (J1, and_1_out, nQ4);
  and and_10 (K1, and_2_out, nQ4);
  and and_11 (and_11_out, Q3, nQ4);
  and and_12 (J2, and_11_out, nQ1);
  and and_13 (K2, and_11_out, Q1);
  and and_14 (and_14_out, and_3_out, nQ2);
  and and_15 (and_15_out, Q2, and_4_out);
  and and_16 (and_16_out, and_3_out, Q2);
  and and_17 (and_17_out, and_4_out, nQ2);
  and and_18 (and_18_out, and_5_out, nQ3);
  and and_19 (and_19_out, and_6_out, Q3);
  and and_20 (and_20_out, and_7_out, nQ3);
  and and_21 (and_21_out, and_8_out, Q3);
  and and_22 (and_22_out, and_5_out, Q3);
  and and_23 (and_23_out, and_6_out, nQ3);
  and and_24 (and_24_out, and_7_out, Q3);
  and and_25 (and_25_out, and_8_out, nQ3);
  or or_1 (J3, and_14_out, and_15_out);
  or or_2 (K3, and_16_out, and_17_out);
  or or_3 (or_3_out, and_18_out, and_19_out);
  or or_4 (J4, or_3_out, or_5_out);
  or or_5 (or_5_out, and_20_out, and_21_out);
  or or_6 (or_6_out, and_22_out, and_23_out);
  or or_7 (K4, or_6_out, or_8_out);
  or or_8 (or_8_out, and_24_out, and_25_out);
  J_K_Flip_Flop u_Q3 (.J(J3), .clk(clock_1_out), .K(K3), .Q(Q3), .Qn(nQ3));  // open: preset, en, reset
  J_K_Flip_Flop u_Q4 (.J(J4), .clk(clock_1_out), .K(K4), .Q(Q4), .Qn(nQ4));  // open: preset, en, reset
  Hex_Digit_Display hex_digit_display_1 (.value({Q1, Q2, Q3, Q4}));  // open: dp
endmodule
