// Logisim project SOP_POS.circ as structural Verilog: 1 circuit, main circuit main
module main (
  output QA1,
  output Error,
  output QA2,
  output QB1,
  output Error2,
  output QB2
);

  wire A, and_1_out, and_2_out, and_3_out, and_4_out, and_5_out, and_6_out, and_7_out, and_8_out, B,
       button_1_out, C, not_1_out, not_2_out, not_3_out, not_4_out, not_5_out, not_6_out, not_7_out,
       not_8_out, or_1_out, or_2_out, or_3_out, or_4_out, or_5_out, or_7_out;

  Button button_1 (.out(button_1_out));
  Counter #(.width(3), .max('h7)) counter_1 (.Q({A, B, C}), .clk(button_1_out));  // open: load, D, count, carry, clr
  not not_1 (not_1_out, A);
  not not_2 (not_2_out, B);
  not not_3 (not_3_out, C);
  not not_4 (not_4_out, A);
  not not_5 (not_5_out, B);
  not not_6 (not_6_out, C);
  and and_1 (and_1_out, A, B);
  not not_7 (not_7_out, B);
  and and_2 (and_2_out, not_7_out, C);
  or or_1 (or_1_out, not_1_out, not_2_out);
  or or_2 (or_2_out, B, not_3_out);
  and and_3 (and_3_out, A, B);
  not not_8 (not_8_out, B);
  and and_4 (and_4_out, not_8_out, C);
  and and_5 (and_5_out, C, A);
  or or_3 (or_3_out, not_4_out, not_5_out);
  or or_4 (or_4_out, B, not_6_out);
  or or_5 (or_5_out, not_4_out, not_6_out);
  or or_6 (QA1, and_1_out, and_2_out);
  and and_6 (and_6_out, or_1_out, or_2_out);
  not not_9 (QA2, and_6_out);
  or or_7 (or_7_out, and_3_out, and_4_out);
  and and_7 (and_7_out, or_3_out, or_4_out);
  or or_8 (QB1, or_7_out, and_5_out);
  and and_8 (and_8_out, and_7_out, or_5_out);
  not not_10 (QB2, and_8_out);
  xor xor_1 (Error, QA1, QA2);
  xor xor_2 (Error2, QB1, QB2);

  // Notes on the sheet:
  //   A B + ~B C
  //   ~((~A + ~B) (B + ~C))
  //   A B + ~B C + A C
  //   ~((~A + ~B) (B + ~C)(~A + ~C))
endmodule
