// Logisim project SOP_to_POS_Conversion.circ as structural Verilog: 1 circuit, main circuit main
module main (
  input  A,
  input  B,
  input  C,
  input  D,
  output Q,
  output out_6
);

  wire and_1_out, and_2_out, and_3_out, and_4_out, and_5_out, not_1_out, not_2_out, not_3_out, not_4_out,
       or_1_out, or_2_out, or_3_out, or_4_out;

  not not_1 (not_1_out, C);
  not not_2 (not_2_out, A);
  or or_1 (or_1_out, not_2_out, not_4_out);
  not not_3 (not_3_out, B);
  or or_2 (or_2_out, not_3_out, not_4_out);
  or or_3 (or_3_out, C, not_4_out);
  not not_4 (not_4_out, D);
  and and_1 (and_1_out, A, D);
  and and_2 (and_2_out, not_1_out, D);
  and and_3 (and_3_out, B, D);
  and and_4 (and_4_out, or_1_out, or_2_out);
  and and_5 (and_5_out, and_4_out, or_3_out);
  or or_4 (or_4_out, and_1_out, and_2_out);
  or or_5 (Q, or_4_out, and_3_out);
  not not_5 (out_6, and_5_out);

  // Notes on the sheet:
  //   SOP to POS Conversion
  //   AD + C'D + BD
  //   ((A' + D') (C + D') (B' + D'))'
endmodule
